# Fritzing sketch air-conditioner (saved by Fritzing 0.9.3b)
breadboards: 1

parts:
  Raspberry_Pi = Raspberry Pi 3 [part_number=RPI-3-V1.2]
  IR_Receiver = TSOP312.., 314.. [part_number=TSOP38238 package=THT]
  Transistor = NPN-Transistor [part_number=P2N2222AG package="TO92 [THT]"]
  IR_LED1 = LTE-302 [part_number=IR333C package=lte-302]
  part = Resistor [tolerance=±5% resistance=10k package=THT]
  part_2 = Resistor [tolerance=±5% resistance=68 package=THT]
  part_3 = Resistor [tolerance=±5% resistance=2.2k package=THT]

nets:
  3V3: Raspberry_Pi.3v3, Raspberry_Pi.3V3, IR_Receiver.Vs
  N1: Raspberry_Pi.GIPO21, IR_Receiver.Data
  N2: Raspberry_Pi.GND, Transistor.E
  N3: Raspberry_Pi.GIPO23, part.Pin_0, part_3.Pin_0
  N4: Raspberry_Pi.5V, part_2.Pin_0
  GND: IR_Receiver.GND, part.Pin_1
  N5: Transistor.B, part_3.Pin_1
  N6: Transistor.C, IR_LED1.C
  N7: IR_LED1.A, part_2.Pin_1
